// Logisim project alu.circ as structural Verilog: 1 circuit, main circuit main
module main (
  input  [31:0] X,
  input  [31:0] Y,
  input  [5:0] Switch__S,
  output Signed_Overflow,
  output [31:0] RESULT,
  output Equal
);

  wire adder_1_cout, adder_2_cout, and_2_out, and_3_out, and_4_out, comparator_1_lt, comparator_2_lt,
       comparator_3_eq, not_1_out, not_2_out, not_3_out, not_4_out, xor_1_out, xor_2_out, xor_3_out;
  wire [4:0] bit_extender_6_out, bit_extender_7_out, bit_extender_8_out;
  wire [30:0] bit_extender_4_out, bit_extender_5_out;
  wire [31:0] Add, And, Bitpal, Lfsr, multiplexer_1_out, multiplexer_3_out, Or, sll, Slt, Sltu, sra, srl, Sub;

  Comparator #(.width(32)) comparator_1 (.a(X), .b(Y), .eq(Equal), .lt(comparator_1_lt));  // open: gt
  Comparator #(.width(32), .mode("unsigned")) comparator_2 (.a(X), .b(Y), .lt(comparator_2_lt));  // open: gt, eq
  assign Sltu = {{31{1'b0}}, comparator_2_lt};  // Bit_Extender bit_extender_1
  Comparator #(.width(16)) comparator_3 (
    .a(X[31:16]),
    .b({X[0], X[1], X[2], X[3], X[4], X[5], X[6], X[7], X[8], X[9], X[10], X[11], X[12], X[13], X[14], X[15]}),
    .eq(comparator_3_eq));  // open: gt, lt
  assign And = X & Y;  // AND_Gate and_1, 32 bits wide
  assign Slt = {{31{1'b0}}, comparator_1_lt};  // Bit_Extender bit_extender_2
  assign Bitpal = {{31{1'b0}}, comparator_3_eq};  // Bit_Extender bit_extender_3
  not not_1 (not_1_out, Switch__S[4]);
  not not_2 (not_2_out, Switch__S[3]);
  not not_3 (not_3_out, Switch__S[2]);
  not not_4 (not_4_out, Switch__S[0]);
  assign Or = X | Y;  // OR_Gate or_1, 32 bits wide
  Bit_Extender #(.in_width(32), .out_width(31)) bit_extender_4 (.in(X), .out(bit_extender_4_out));
  Bit_Extender #(.in_width(32), .out_width(31)) bit_extender_5 (.in(Y), .out(bit_extender_5_out));
  Subtractor #(.width(32)) subtractor_1 (.a(X), .b(Y), .out(Sub));  // open: bin, bout
  and and_2 (and_2_out, Switch__S[5], not_1_out, not_2_out, not_3_out, not_4_out);
  Bit_Extender #(.in_width(32), .out_width(5)) bit_extender_6 (.in(Y), .out(bit_extender_6_out));
  Bit_Extender #(.in_width(32), .out_width(5)) bit_extender_7 (.in(Y), .out(bit_extender_7_out));
  Bit_Extender #(.in_width(32), .out_width(5)) bit_extender_8 (.in(Y), .out(bit_extender_8_out));
  Adder #(.width(31)) adder_1 (.a(bit_extender_4_out), .b(bit_extender_5_out), .cout(adder_1_cout));  // open: out, cin
  Adder #(.width(32)) adder_2 (.a(X), .b(Y), .out(Add), .cout(adder_2_cout));  // open: cin
  Shifter #(.width(32)) shifter_1 (.in(X), .\dist (bit_extender_6_out), .out(sll));
  Shifter #(.width(32), .shift("lr")) shifter_2 (.in(X), .\dist (bit_extender_7_out), .out(srl));
  Shifter #(.width(32), .shift("ar")) shifter_3 (.in(X), .\dist (bit_extender_8_out), .out(sra));
  and and_3 (and_3_out, adder_1_cout, and_2_out);
  and and_4 (and_4_out, adder_2_cout, and_2_out);
  assign Lfsr = {{31{1'b0}}, xor_3_out};  // Bit_Extender bit_extender_9
  or or_2 (Signed_Overflow, and_3_out, and_4_out);
  xor xor_1 (xor_1_out, X[0], X[2]);
  xor xor_2 (xor_2_out, xor_1_out, X[3]);
  xor xor_3 (xor_3_out, xor_2_out, X[5]);
  Multiplexer #(.select(2), .width(32)) multiplexer_1 (
    .in0(sll), .in2(srl), .in3(sra), .out(multiplexer_1_out), .sel(Switch__S[1:0]));  // open: in1, en
  Multiplexer #(.width(32)) multiplexer_2 (
    .in0(multiplexer_1_out), .in1(multiplexer_3_out), .out(RESULT), .sel(Switch__S[5]));  // open: en
  Multiplexer #(.select(5), .width(32)) multiplexer_3 (
    .in0(Add), .in1(Add), .in2(Sub), .in3(Sub), .in4(And), .in5(Or), .in10(Slt), .in11(Sltu), .in16(Sltu),
    .in30(Bitpal), .in31(Lfsr), .out(multiplexer_3_out), .sel(Switch__S[4:0]));  // open: in6, in7, in8, in9, in12, in13, in14, in15, in17, in18, in19, in20, in21, in22, in23, in24, in25, in26, in27, in28, in29, en

  // Other names for the same wires on the sheet: _2 = Switch__S[2]; Switch[5:0] = Switch__S; _3 = Switch__S[3];
  //   _4 = Switch__S[4]; _0 = Switch__S[0]; _1 = Switch__S[1]; EQ = Equal; OF = Signed_Overflow; _5 = Switch__S[5]

  // Notes on the sheet:
  //   INPUTS to your circuit
  //   INPUT to your circuit
  //   DON'T CHANGE THE INPUTS AND OUTPUTS! IF YOU DO SO, YOU NEED TO MAKE SURE THE PINS ARE IN THE RIGHT PLACES!
  //   OUTPUTS of your circuit
endmodule
