// Logisim project mem.circ as structural Verilog: 1 circuit, main circuit main
module main (
  input  [31:0] Data_Mem_Addr,
  input  [31:0] Data_Mem_In,
  input  ACCESS_BYTE,
  input  MEM_WRITE,
  input  CLOCK,
  output [31:0] Data_Mem_Out
);

  wire not_1_out;
  wire [1:0] Selector;
  wire [4:0] bit_extender_2_out;
  wire [31:0] B, Data, shifter_1_out, subtractor_1_out;

  assign Data = MEM_WRITE ? Data_Mem_In : 32'bz;  // Controlled_Buffer controlled_buffer_1
  Bit_Extender #(.in_width(32), .out_width(2)) bit_extender_1 (.in(Data_Mem_Addr), .out(Selector));
  Subtractor #(.width(32)) subtractor_1 (
    .a(Data_Mem_Addr), .b(32'h10010000), .out(subtractor_1_out));  // open: bin, bout
  assign bit_extender_2_out = {{3{1'b0}}, Selector};  // Bit_Extender bit_extender_2
  Shifter #(.width(32), .shift("lr")) shifter_1 (.in(Data), .\dist (bit_extender_2_out), .out(shifter_1_out));
  not not_1 (not_1_out, MEM_WRITE);
  assign B = 32'h1 & shifter_1_out;  // AND_Gate and_1, 32 bits wide
  RAM #(.addrWidth(24), .dataWidth(32)) ram_1 (
    .addr(subtractor_1_out[25:2]), .data(Data), .sel(1'b1), .clk(CLOCK), .ld(not_1_out), .clr(1'b0));
  Multiplexer #(.width(32)) multiplexer_1 (.in0(Data), .in1(B), .out(Data_Mem_Out), .sel(ACCESS_BYTE));  // open: en

  // Other names for the same wires on the sheet: A = ACCESS_BYTE; C = CLOCK; E = MEM_WRITE

  // Notes on the sheet:
  //   These are INPUTS to the circuit
  //   These are INPUTS to the circuit
  //   DO NOT CHANGE THE LOCATIONS OF THE INPUTS/OUTPUTS! IF YOU DO SO, YOU NEED TO MAKE SURE THE PINS ARE AT THE RIGHT PLACE!
  //   Yet again, the clock is not an actual clock, but an input, one that will be driven from a higher circuit
  //   This is an OUTPUT to the circuit
endmodule
