// Logisim project cpu.circ as structural Verilog: 1 circuit, main circuit main
module main (
  input  [31:0] RS_READ_VALUE,
  input  [31:0] RT_READ_VALUE,
  input  [31:0] INSTRUCTION,
  input  CLOCK,
  input  RESET,
  output [31:0] t0,
  output [31:0] t1,
  output [31:0] t2,
  output [31:0] t3,
  output [4:0] RS,
  output [4:0] RT,
  output [4:0] Write_Register,
  output [31:0] RD_WRITE_VALUE,
  output RD_WRITE_ENABLE,
  output [23:0] FETCH_ADDRESS
);

  wire accessByte, ALU_signed_overflow, ALUSrc, and_6_out, and_7_out, and_9_out, and_10_out, and_12_out,
       and_13_out, and_14_out, beq, bne, Branch, comparator_1_eq, comparator_2_eq, comparator_3_eq,
       comparator_4_eq, comparator_5_eq, comparator_8_eq, comparator_9_eq, comparator_10_eq,
       comparator_11_eq, comparator_12_eq, comparator_13_eq, comparator_14_eq, comparator_16_eq,
       comparator_18_eq, comparator_19_eq, comparator_20_eq, comparator_21_eq, comparator_22_eq,
       comparator_23_eq, comparator_24_eq, comparator_25_eq, comparator_26_eq, comparator_27_eq,
       comparator_28_eq, comparator_29_eq, comparator_30_eq, is_lui, isShift, jl, js, jump, Kill, MemToReg,
       MemWr, nori, not_1_out, not_2_out, not_3_out, not_4_out, not_5_out, not_6_out, not_7_out, not_8_out,
       not_9_out, not_10_out, not_11_out, not_12_out, not_13_out, not_14_out, not_15_out, not_16_out,
       not_17_out, not_18_out, not_19_out, not_20_out, not_21_out, not_22_out, not_23_out, or_2_out,
       or_3_out, or_4_out, or_7_out, or_9_out, or_10_out, RD_RT, Zero;
  wire [1:0] bit_extender_5_out, bit_extender_6_out, bit_extender_9_out, op_f_4_5;
  wire [3:0] op_f_0_3;
  wire [5:0] ALUctr, funct, multiplexer_12_out, multiplexer_13_out, multiplexer_14_out;
  wire [23:0] addr;
  wire [31:0] adder_1_out, ALU_input_X, ALU_input_Y, ALU_result, bit_extender_2_out, bit_extender_4_out,
       bit_extender_7_out, bit_extender_8_out, bit_extender_10_out, bit_extender_11_out, Imm, jsaddr,
       MEM_data_mem_out, multiplexer_1_out, multiplexer_3_out, multiplexer_5_out, multiplexer_6_out,
       multiplexer_8_out, multiplexer_9_out, multiplexer_10_out, multiplexer_11_out, multiplexer_15_out,
       PC_1, PCOut, Read_Data_1, Read_Data_2, subtractor_1_out;
  wire [31:6] In;

  Bit_Extender #(.in_width(32), .out_width(24)) bit_extender_1 (.in(PCOut), .out(FETCH_ADDRESS));
  not not_1 (not_1_out, In[27]);
  not not_2 (not_2_out, In[28]);
  not not_3 (not_3_out, In[29]);
  not not_4 (not_4_out, In[30]);
  not not_5 (not_5_out, In[26]);
  not not_6 (not_6_out, In[31]);
  and and_1 (RD_RT, not_6_out, not_4_out, not_3_out, not_2_out, not_1_out, not_5_out);
  not not_7 (not_7_out, In[29]);
  not not_8 (not_8_out, In[28]);
  not not_9 (not_9_out, In[30]);
  and and_2 (MemToReg, In[31], not_9_out, not_7_out, not_8_out, In[27], In[26]);
  Comparator #(.width(6), .mode("unsigned")) comparator_1 (
    .a(In[31:26]), .b(6'b101011), .eq(comparator_1_eq));  // open: gt, lt
  Comparator #(.width(6), .mode("unsigned")) comparator_2 (
    .a(funct), .b(6'b001000), .eq(comparator_2_eq));  // open: gt, lt
  Comparator #(.width(6), .mode("unsigned")) comparator_3 (
    .a(In[31:26]), .b({6{1'b0}}), .eq(comparator_3_eq));  // open: gt, lt
  Comparator #(.width(6), .mode("unsigned")) comparator_4 (
    .a(In[31:26]), .b(6'b000010), .eq(comparator_4_eq));  // open: gt, lt
  Comparator #(.width(6), .mode("unsigned")) comparator_5 (
    .a(In[31:26]), .b(6'b000011), .eq(comparator_5_eq));  // open: gt, lt
  Comparator #(.width(6), .mode("unsigned")) comparator_6 (.a(In[31:26]), .b(6'b000100), .eq(beq));  // open: gt, lt
  Comparator #(.width(6), .mode("unsigned")) comparator_7 (.a(In[31:26]), .b(6'b000101), .eq(bne));  // open: gt, lt
  not not_10 (not_10_out, In[28]);
  not not_11 (not_11_out, In[30]);
  and and_3 (MemWr, In[31], not_11_out, In[29], not_10_out, In[27], In[26]);
  and and_4 (js, comparator_2_eq, comparator_3_eq);
  not not_12 (not_12_out, Zero);
  assign bit_extender_2_out = {{31{1'b0}}, 1'b0};  // Bit_Extender bit_extender_2
  not not_13 (not_13_out, In[26]);
  not not_14 (not_14_out, In[31]);
  not not_15 (not_15_out, In[27]);
  not not_16 (not_16_out, In[29]);
  not not_17 (not_17_out, In[30]);
  and and_5 (Branch, not_14_out, not_17_out, not_16_out, In[28], not_15_out, not_13_out);
  or or_1 (jl, comparator_5_eq, comparator_4_eq);
  or or_2 (or_2_out, comparator_1_eq, js, comparator_4_eq, beq, bne);
  Adder #(.width(32)) adder_1 (.a(PC_1), .b(Imm), .out(adder_1_out));  // open: cin, cout
  and and_6 (and_6_out, Zero, beq);
  and and_7 (and_7_out, not_12_out, bne);
  Bit_Extender #(.in_width(32), .out_width(24)) bit_extender_3 (.in({In[31:26], RS, RT, In[15:6], funct}), .out(addr));
  Multiplexer #(.width(32)) multiplexer_1 (
    .in0(INSTRUCTION), .in1(bit_extender_2_out), .out(multiplexer_1_out), .sel(Kill));  // open: en
  or or_3 (or_3_out, MemToReg, MemWr);
  not not_18 (not_18_out, or_2_out);
  assign bit_extender_4_out = {{8{1'b0}}, addr};  // Bit_Extender bit_extender_4
  Subtractor #(.width(32)) subtractor_1 (.a(adder_1_out), .b(32'h1), .out(subtractor_1_out));  // open: bin, bout
  or or_4 (or_4_out, and_6_out, and_7_out);
  or or_5 (Kill, jump, or_4_out);
  Register #(.width(32)) register_1 (
    .D(multiplexer_1_out), .Q({In[31:26], RS, RT, In[15:6], funct}), .clk(CLOCK));  // open: en, clr
  Multiplexer #(.width(6)) multiplexer_2 (
    .in0(In[31:26]), .in1(funct), .out({op_f_4_5, op_f_0_3}), .sel(comparator_8_eq));  // open: en
  Comparator #(.width(1)) comparator_8 (.a(RD_RT), .b(1'b1), .eq(comparator_8_eq));  // open: gt, lt
  and and_8 (RD_WRITE_ENABLE, not_18_out, not_19_out);
  not not_19 (not_19_out, comparator_9_eq);
  Comparator #(.width(32), .mode("unsigned")) comparator_9 (
    .a({In[31:26], RS, RT, In[15:6], funct}), .b({32{1'b0}}), .eq(comparator_9_eq));  // open: gt, lt
  Multiplexer #(.width(32)) multiplexer_3 (
    .in0(PC_1), .in1(subtractor_1_out), .out(multiplexer_3_out), .sel(or_4_out));  // open: en
  not not_20 (not_20_out, nori);
  Bit_Extender #(.in_width(5), .out_width(2)) bit_extender_5 (.in(RT), .out(bit_extender_5_out));
  Bit_Extender #(.in_width(5), .out_width(2)) bit_extender_6 (.in(RS), .out(bit_extender_6_out));
  Multiplexer #(.width(5)) multiplexer_4 (.in0(RT), .in1(In[15:11]), .out(Write_Register), .sel(RD_RT));  // open: en
  not not_21 (not_21_out, RD_RT);
  not not_22 (not_22_out, beq);
  not not_23 (not_23_out, bne);
  Multiplexer #(.width(32)) multiplexer_5 (
    .in0(multiplexer_3_out), .in1(multiplexer_6_out), .out(multiplexer_5_out), .sel(jump));  // open: en
  or or_6 (jump, jl, js);
  Multiplexer #(.width(32)) multiplexer_6 (
    .in0(bit_extender_4_out), .in1(jsaddr), .out(multiplexer_6_out), .sel(js));  // open: en
  Subtractor #(.width(32)) subtractor_2 (.a(Read_Data_1), .b(32'h100000), .out(jsaddr));  // open: bin, bout
  assign bit_extender_7_out = {{16{1'b0}}, {In[15:6], funct}};  // Bit_Extender bit_extender_7
  assign bit_extender_8_out = {{16{In[15]}}, {In[15:6], funct}};  // Bit_Extender bit_extender_8
  and and_9 (and_9_out, In[15], not_20_out);
  Bit_Extender #(.in_width(5), .out_width(2)) bit_extender_9 (.in(Write_Register), .out(bit_extender_9_out));
  or or_7 (or_7_out, or_3_out, not_21_out);
  and and_10 (and_10_out, not_22_out, not_23_out);
  Multiplexer #(.width(32)) multiplexer_7 (
    .in0(bit_extender_7_out), .in1(bit_extender_8_out), .out(Imm), .sel(and_9_out));  // open: en
  regfile_main RegFile (
    .Read_register_1(bit_extender_6_out), .Read_register_2(bit_extender_5_out),
    .write_register(bit_extender_9_out), .write_data(RD_WRITE_VALUE), .t0_Value(t0), .t1_Value(t1),
    .t2_Value(t2), .t3_Value(t3), .RegWrite(RD_WRITE_ENABLE), .clock(CLOCK), .Read_Data_1(Read_Data_1),
    .Read_Data_2(Read_Data_2));
  and and_11 (ALUSrc, or_7_out, and_10_out);
  Comparator #(.width(6), .mode("unsigned")) comparator_10 (
    .a(In[31:26]), .b({6{1'b0}}), .eq(comparator_10_eq));  // open: gt, lt
  Comparator #(.width(6), .mode("unsigned")) comparator_11 (
    .a(In[31:26]), .b({6{1'b0}}), .eq(comparator_11_eq));  // open: gt, lt
  and and_12 (and_12_out, comparator_11_eq, comparator_12_eq);
  Comparator #(.width(6), .mode("unsigned")) comparator_12 (
    .a(funct), .b(6'b000011), .eq(comparator_12_eq));  // open: gt, lt
  Comparator #(.width(6), .mode("unsigned")) comparator_13 (
    .a(In[31:26]), .b({6{1'b0}}), .eq(comparator_13_eq));  // open: gt, lt
  and and_13 (and_13_out, comparator_13_eq, comparator_14_eq);
  Comparator #(.width(6), .mode("unsigned")) comparator_14 (
    .a(funct), .b({6{1'b0}}), .eq(comparator_14_eq));  // open: gt, lt
  Register #(.width(32)) PC (.D(multiplexer_5_out), .Q(PCOut), .clk(CLOCK));  // open: en, clr
  assign bit_extender_10_out = {{27{1'b0}}, 5'b00001};  // Bit_Extender bit_extender_10
  Comparator #(.width(6), .mode("unsigned")) comparator_15 (.a(In[31:26]), .b(6'b001101), .eq(nori));  // open: gt, lt
  and and_14 (and_14_out, comparator_10_eq, comparator_16_eq);
  Comparator #(.width(6), .mode("unsigned")) comparator_16 (
    .a(funct), .b(6'b000010), .eq(comparator_16_eq));  // open: gt, lt
  Adder #(.width(32)) adder_2 (.a(PCOut), .b(bit_extender_10_out), .out(PC_1));  // open: cin, cout
  Multiplexer #(.width(32)) multiplexer_8 (
    .in0(ALU_input_Y), .in1(Imm), .out(multiplexer_8_out), .sel(ALUSrc));  // open: en
  Multiplexer #(.width(32)) multiplexer_9 (
    .in0(multiplexer_8_out), .in1(32'h10), .out(multiplexer_9_out), .sel(is_lui));  // open: en
  assign bit_extender_11_out = {{27{1'b0}}, In[10:6]};  // Bit_Extender bit_extender_11
  Comparator #(.width(6), .mode("unsigned")) comparator_17 (.a(In[31:26]), .b(6'b001111), .eq(is_lui));  // open: gt, lt
  or or_8 (isShift, and_14_out, and_12_out, and_13_out);
  Comparator #(.width(5)) comparator_18 (.a(RS), .b(5'b01000), .eq(comparator_18_eq));  // open: gt, lt
  Comparator #(.width(5)) comparator_19 (.a(RS), .b(5'b01001), .eq(comparator_19_eq));  // open: gt, lt
  Comparator #(.width(5)) comparator_20 (.a(RS), .b(5'b01010), .eq(comparator_20_eq));  // open: gt, lt
  Comparator #(.width(5)) comparator_21 (.a(RS), .b(5'b01011), .eq(comparator_21_eq));  // open: gt, lt
  Multiplexer #(.width(32)) multiplexer_10 (
    .in0(ALU_input_X), .in1(ALU_input_Y), .out(multiplexer_10_out), .sel(isShift));  // open: en
  Multiplexer #(.width(32)) multiplexer_11 (
    .in0(multiplexer_9_out), .in1(bit_extender_11_out), .out(multiplexer_11_out), .sel(isShift));  // open: en
  or or_9 (or_9_out, comparator_18_eq, comparator_19_eq, comparator_20_eq, comparator_21_eq);
  LED led_1 (.in(ALU_signed_overflow));
  alu_main ALU (
    .Switch__S(ALUctr), .X(multiplexer_10_out), .Equal(Zero), .RESULT(ALU_result),
    .Signed_Overflow(ALU_signed_overflow), .Y(multiplexer_11_out));
  Multiplexer #(.select(4), .width(6)) multiplexer_12 (
    .in0({6{1'b0}}), .in2(6'b000010), .in3(6'b000011), .in9(6'b100000), .in12(6'b100100), .in13(6'b100101),
    .in15({6{1'b0}}), .out(multiplexer_12_out), .sel(op_f_0_3));  // open: in1, in4, in5, in6, in7, in8, in10, in11, in14, en
  Multiplexer #(.select(4), .width(6)) multiplexer_13 (
    .in0(6'b100000), .in1(6'b100001), .in2(6'b100010), .in3(6'b100011), .in4(6'b100100), .in5(6'b100101),
    .in10(6'b101010), .in11(6'b101011), .out(multiplexer_13_out), .sel(op_f_0_3));  // open: in6, in7, in8, in9, in12, in13, in14, in15, en
  Multiplexer #(.select(4), .width(6)) multiplexer_14 (
    .in14(6'b111110), .in15({6{1'b1}}), .out(multiplexer_14_out), .sel(op_f_0_3));  // open: in0, in1, in2, in3, in4, in5, in6, in7, in8, in9, in10, in11, in12, in13, en
  Multiplexer #(.width(32)) multiplexer_15 (
    .in0(RS_READ_VALUE), .in1(Read_Data_1), .out(multiplexer_15_out), .sel(or_9_out));  // open: en
  Comparator #(.width(5)) comparator_22 (.a(RT), .b(5'b01000), .eq(comparator_22_eq));  // open: gt, lt
  Comparator #(.width(5)) comparator_23 (.a(RT), .b(5'b01001), .eq(comparator_23_eq));  // open: gt, lt
  Comparator #(.width(5)) comparator_24 (.a(RT), .b(5'b01010), .eq(comparator_24_eq));  // open: gt, lt
  Comparator #(.width(5)) comparator_25 (.a(RT), .b(5'b01011), .eq(comparator_25_eq));  // open: gt, lt
  or or_10 (or_10_out, comparator_22_eq, comparator_23_eq, comparator_24_eq, comparator_25_eq);
  Multiplexer #(.select(2), .width(6)) multiplexer_16 (
    .in0(multiplexer_12_out), .in2(multiplexer_13_out), .in3(multiplexer_14_out), .out(ALUctr), .sel(op_f_4_5));  // open: in1, en
  Multiplexer #(.width(32)) multiplexer_17 (
    .in0(multiplexer_15_out), .in1(Imm), .out(ALU_input_X), .sel(is_lui));  // open: en
  Multiplexer #(.width(32)) multiplexer_18 (
    .in0(RT_READ_VALUE), .in1(Read_Data_2), .out(ALU_input_Y), .sel(or_10_out));  // open: en
  Multiplexer #(.width(32)) multiplexer_19 (
    .in0(ALU_result), .in1(MEM_data_mem_out), .out(RD_WRITE_VALUE), .sel(MemToReg));  // open: en
  mem_main MEM (
    .Data_Mem_Addr(ALU_result), .Data_Mem_In(ALU_input_Y), .ACCESS_BYTE(accessByte), .MEM_WRITE(MemWr),
    .CLOCK(CLOCK), .Data_Mem_Out(MEM_data_mem_out));
  Comparator #(.width(6)) comparator_26 (.a(In[31:26]), .b(6'b001111), .eq(comparator_26_eq));  // open: gt, lt
  Comparator #(.width(6)) comparator_27 (.a(In[31:26]), .b(6'b100000), .eq(comparator_27_eq));  // open: gt, lt
  Comparator #(.width(6)) comparator_28 (.a(In[31:26]), .b(6'b100100), .eq(comparator_28_eq));  // open: gt, lt
  Comparator #(.width(6)) comparator_29 (.a(In[31:26]), .b(6'b100011), .eq(comparator_29_eq));  // open: gt, lt
  Comparator #(.width(6)) comparator_30 (.a(In[31:26]), .b(6'b101011), .eq(comparator_30_eq));  // open: gt, lt
  or or_11 (accessByte, comparator_26_eq, comparator_27_eq, comparator_28_eq, comparator_29_eq, comparator_30_eq);

  // Other names for the same wires on the sheet: In (some bits) = {RS, RT, funct}; shamt[4:0] = In[10:6];
  //   signed = In[15]; a[31:0] = RS_READ_VALUE; b[31:0] = RT_READ_VALUE; C = CLOCK; Data_Mem_In[31:0] = ALU_input_Y;
  //   OP[5:0] = In[31:26]; OP_funct[5:0] = {op_f_4_5, op_f_0_3}; RegDest = RD_RT; RegWr = RD_WRITE_ENABLE;
  //   wd[31:0] = RD_WRITE_VALUE; wr[4:0] = Write_Register

  // Notes on the sheet:
  //   These are outputs/inputs from run.circ
  //   These are outputs to run.circ
  //   Feel free to move these components
endmodule
